# Fritzing sketch button practice wk3 (saved by Fritzing 0.9.4)
breadboards: 1

parts:
  S1 = Pushbutton [package="[THT]"]
  R1 = Resistor [tolerance=±5% resistance=220 package=THT]
  元件1 = Adafruit Circuit Playground Express [part_number="Adafruit #3333"]

nets:
  N1: S1.Pin_1, S1.Pin_2, 元件1.3.3V
  N2: S1.Pin_3, S1.Pin_4, R1.Pin_1, 元件1.D6_A1
  N3: R1.Pin_0, 元件1.GND

custom parts:
  Adafruit Circuit Playground Express: Circuit Playground Express is the next step towards a perfect introduction to electronics and programming. We've taken the original Circuit Playground Classic and made it even better! Not only did we pack even more sensors in, we also made it even easier to program. You can now start your journey with Microsoft MakeCode block-based or Javascript programming. Then, you can use the same board to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
