# Fritzing sketch input practice (saved by Fritzing 0.9.4)
breadboards: 1

parts:
  R2 = Resistor [tolerance=±5% resistance=10 package=THT]
  S1 = Toggle Switch [package=THT]
  元件2 = Adafruit Circuit Playground Express [part_number="Adafruit #3333"]

nets:
  N1: R2.Pin_0, S1.L2
  N2: R2.Pin_1, 元件2.3.3V
  N3: S1.L1, 元件2.GND
  N4: S1.COM, 元件2.D6_A1

custom parts:
  Adafruit Circuit Playground Express: Circuit Playground Express is the next step towards a perfect introduction to electronics and programming. We've taken the original Circuit Playground Classic and made it even better! Not only did we pack even more sensors in, we also made it even easier to program. You can now start your journey with Microsoft MakeCode block-based or Javascript programming. Then, you can use the same board to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
